# Fritzing sketch nrf24l01_comms (saved by Fritzing 0.9.7b)
circuit board: 4.21892cm x 7.82012cm

parts:
  Nano1 = Arduino Nano v2.3
  Part1 = Adafruit PowerBoost 1000C [part_number="Adafruit #2465"]
  Part2 = NRF24L01+ Breakout Board
  C1 = Electrolytic Capacitor [capacitance=10μF voltage=20V package="0405 [SMD, electrolytic]"]
  DHT2 = DHT11 Humitidy and Temperature Sensor (3 pins)

nets:
  GND: Nano1.GND, Part1.GND, Part2.GND, C1.-, DHT2.GND
  N1: Nano1.D4, DHT2.VDD
  N2: Nano1.D9, Part2.CS
  N3: Nano1.D10, Part2.CE
  N4: Nano1.D11, Part2.MOSI
  N5: Nano1.D12, Part2.MISO
  N6: Nano1.D13, Part2.SCK
  3V3: Nano1.3V3, Part2.VCC, C1.+
  N7: Nano1.+5V, DHT2.DATA
  N8: Nano1.VIN, Part1.5.0V

custom parts:
  Adafruit PowerBoost 1000C: PowerBoost 1000C is the perfect power supply for your portable project! With a built-in load-sharing battery charger circuit, you'll be able to keep your power-hungry project running even while recharging the battery! This little DC/DC boost converter module can be powered by any 3.7V LiIon/LiPoly battery, and convert the battery output to 5.2V DC for running your 5V projects.
  DHT11 Humitidy and Temperature Sensor (3 pins): DHT11 Humidity and Temperature Sensor (3 pins) from the design created by John De Cristofaro for Adafruit Industries.
